// Logisim project cpu.circ as structural Verilog: 2 circuits, main circuit CPU
module CPU (
  input  [31:0] Instruction,
  input  CLK,
  output [31:0] s0,
  output [31:0] s1,
  output [31:0] t0,
  output [31:0] t1,
  output [31:0] a0,
  output [31:0] ra,
  output [31:0] sp,
  output [31:0] PC
);

  wire Asel, Bsel, main_1_p1, main_1_p2, main_1_p6, PCsel, WE;
  wire [3:0] undriven;
  wire [31:0] A, B, Imm, jump, multiplexer_1_out, PC___4, PC_t, R1, R2, ResulAlu, W;

  // Incrementer incrementer_1: pin names not known; wires that end beside it: Instruction, jump, PC, PC___4
  Multiplexer #(.width(32), .enable("false")) multiplexer_1 (
    .in0(PC___4), .in1(ResulAlu), .out(multiplexer_1_out), .sel(PCsel));
  // PC pc_1: pin names not known; wires that end beside it: multiplexer_1_out, CLK, PC
  jump jump_1 ();
  RegFile regfile_1 (
    .Clk(CLK), .R1(R1), .R2(R2), .WE(WE), .W(W), .RD(Instruction[11:7]), .RS1(Instruction[19:15]),
    .RS2(Instruction[24:20]), .s0(s0), .s1(s1), .t0(t0), .t1(t1), .a0(a0), .ra(ra), .sp(sp));
  Multiplexer #(.width(32), .enable("false")) multiplexer_2 (.in0(PC_t), .in1(R1), .out(A), .sel(Bsel));
  Multiplexer #(.width(32), .enable("false")) multiplexer_3 (.in0(Imm), .in1(R2), .out(B), .sel(Asel));
  ALU alu_1 (.A(A), .B(B), .ALU_Op(undriven), .Out(ResulAlu));
  // memory_main main_1: pin names not known; wires that end beside it: main_1_p1, main_1_p2, main_1_p1, main_1_p2, CLK, main_1_p6, main_1_p6

  // Other names for the same wires on the sheet: fetch_addr[31:0] = PC; INST[31:0] = Instruction;
  //   Opcode[6:0] = Instruction[6:0]; RD[4:0] = Instruction[11:7]; f3[2:0] = Instruction[14:12];
  //   RS1[4:0] = Instruction[19:15]; RS2[4:0] = Instruction[24:20]; f7[6:0] = Instruction[31:25]

  // Notes on the sheet:
  //   NOTE
  //   Please do not modify/replace/move/change/delete/etc input and output pins
  //   These are debug/test outputs from your circuit
endmodule

module jump (
);

  wire undriven;

  Multiplexer #(.enable("false")) multiplexer_1 (.sel(undriven));  // open: in0, in1, out
endmodule
